// Logisim project lab4-q1.circ as structural Verilog: 1 circuit, main circuit main
module main (
  input  A,
  input  B,
  output X
);

  wire and_1_out, and_2_out;

  and and_1 (and_1_out, A, A);
  and and_2 (and_2_out, A, ~A);  // AND_Gate
  or or_1 (X, and_1_out, and_2_out);

  assign B = A;

  // Notes on the sheet:
  //   Brian Kim
endmodule
