// Logisim project lab4-q6.circ as structural Verilog: 1 circuit, main circuit main
module main (
  input  D0,
  input  D1,
  input  S,
  output Y
);

  wire and_1_out, and_2_out;

  and and_1 (and_1_out, D0, ~S);  // AND_Gate
  and and_2 (and_2_out, D1, S);
  or or_1 (Y, and_1_out, and_2_out);

  // Notes on the sheet:
  //   Brian Kim
endmodule
